// Logisim project arbiter.circ as structural Verilog: 10 circuits, main circuit rom
// m3_grnt_
module main (
  input  in_1,
  input  in_2,
  input  in_3,
  input  in_4,
  output out_5,
  output out_6,
  output out_7,
  output out_8
);

  wire bitselector_1_out, clock_1_out;
  wire [2:0] undriven_2;
  wire [7:0] undriven;

  Priority_Encoder priority_encoder_1 ();  // open: in0, in1, in2, in3, in4, in5, in6, in7, out, en_in, gs, en_out
  Clock clock_1 (.out(clock_1_out));
  Multiplexer #(.select(2)) multiplexer_1 ();  // open: in0, in1, in2, in3, out, sel, en
  bus_arbiter bus_arbiter_1 (
    .m3_req_(in_1), .m2_req_(in_2), .m1_req_(in_3), .m0_req_(in_4), .m3_grnt_(out_5), .m2_grnt_(out_6),
    .m1_grnt_(out_7), .m0_grnt_(out_8), .clk(clock_1_out));  // open: reset, out_8, out_7
  Decoder #(.select(2)) decoder_1 ();  // open: out0, out1, out2, out3, sel, en
  spm spm_1 ();  // open: if_spm_as_, if_spm_rw, if_spm_addr, if_spm_wr_data, if_spm_rd_data
  BitSelector bitselector_1 (.in(undriven), .out(bitselector_1_out), .sel(undriven_2));
endmodule

module bus_arbiter (
  input  m3_req_,
  input  m2_req_,
  input  m1_req_,
  input  m0_req_,
  input  clk,
  input  reset,
  output out_7,
  output [1:0] out_8,
  output m3_grnt_,
  output m2_grnt_,
  output m1_grnt_,
  output m0_grnt_
);

  wire demultiplexer_1_out0, demultiplexer_1_out1, demultiplexer_1_out2, demultiplexer_1_out3,
       multiplexer_1_out, multiplexer_2_out, multiplexer_4_out, multiplexer_6_out, or_1_out;
  wire [1:0] multiplexer_3_out, multiplexer_9_out, priority_encoder_2_out, priority_encoder_3_out,
       priority_encoder_4_out, register_1_q;

  Demultiplexer #(.select(2)) demultiplexer_1 (
    .out0(demultiplexer_1_out0), .out1(demultiplexer_1_out1), .out2(demultiplexer_1_out2),
    .out3(demultiplexer_1_out3), .in(1'b1), .sel(register_1_q), .en(or_1_out));
  Clock clock_1 ();  // open: out
  Multiplexer multiplexer_1 (.in0(1'b0), .in1(demultiplexer_1_out0), .out(multiplexer_1_out), .en(1'b1));  // open: sel
  Priority_Encoder #(.select(2)) priority_encoder_1 (
    .in0(m3_req_), .in1(m2_req_), .in2(m1_req_), .in3(m0_req_), .out(out_8));  // open: gs, en_out, en_in
  Multiplexer multiplexer_2 (.in0(1'b0), .in1(demultiplexer_1_out1), .out(multiplexer_2_out), .sel(m1_req_), .en(1'b1));
  Multiplexer #(.select(2), .width(2)) multiplexer_3 (
    .in0(2'b11), .in1(2'b10), .in2(2'b01), .in3(2'b00), .out(multiplexer_3_out), .sel(out_8));  // open: en
  Multiplexer multiplexer_4 (.in0(1'b0), .in1(demultiplexer_1_out2), .out(multiplexer_4_out), .sel(m2_req_), .en(1'b1));
  Priority_Encoder #(.select(2)) priority_encoder_2 (
    .in0(m0_req_), .in1(m3_req_), .in2(m2_req_), .in3(m1_req_), .out(priority_encoder_2_out),
    .en_in(demultiplexer_1_out1));  // open: gs, en_out
  Multiplexer #(.select(2), .width(2)) multiplexer_5 (
    .in0(2'b00), .in1(2'b11), .in2(2'b10), .in3(2'b01), .out(multiplexer_3_out),
    .sel(priority_encoder_2_out), .en(demultiplexer_1_out1));
  Multiplexer multiplexer_6 (.in0(1'b0), .in1(demultiplexer_1_out3), .out(multiplexer_6_out), .sel(m3_req_), .en(1'b1));
  Priority_Encoder #(.select(2)) priority_encoder_3 (
    .in0(m1_req_), .in1(m0_req_), .in2(m3_req_), .in3(m2_req_), .out(priority_encoder_3_out),
    .en_in(demultiplexer_1_out2));  // open: gs, en_out
  Register #(.width(1)) u_m0_grnt_ (.D(multiplexer_1_out), .en(1'b1), .Q(m0_grnt_), .clk(clk), .clr(reset));
  Multiplexer #(.select(2), .width(2)) multiplexer_7 (
    .in0(2'b01), .in1(2'b00), .in2(2'b11), .in3(2'b10), .out(multiplexer_3_out),
    .sel(priority_encoder_3_out), .en(demultiplexer_1_out2));
  Register #(.width(1)) u_m1_grnt_ (.D(multiplexer_2_out), .en(1'b1), .Q(m1_grnt_), .clk(clk), .clr(reset));
  Priority_Encoder #(.select(2)) priority_encoder_4 (
    .in0(m2_req_), .in1(m1_req_), .in2(m0_req_), .in3(m3_req_), .out(priority_encoder_4_out),
    .en_in(demultiplexer_1_out3));  // open: gs, en_out
  Register #(.width(1)) u_m2_grnt_ (.D(multiplexer_4_out), .en(1'b1), .Q(m2_grnt_), .clk(clk), .clr(reset));
  Multiplexer #(.select(2), .width(2)) multiplexer_8 (
    .in0(2'b10), .in1(2'b01), .in2(2'b00), .in3(2'b11), .out(multiplexer_3_out),
    .sel(priority_encoder_4_out), .en(demultiplexer_1_out3));
  Register #(.width(1)) u_m3_grnt_ (.D(multiplexer_6_out), .en(1'b1), .Q(m3_grnt_), .clk(clk), .clr(reset));
  Multiplexer #(.width(2)) multiplexer_9 (
    .in0(2'b00), .in1(multiplexer_3_out), .out(multiplexer_9_out), .sel(or_1_out), .en(1'b1));
  Register #(.width(2)) register_1 (.D(multiplexer_9_out), .en(1'b1), .Q(register_1_q), .clk(clk), .clr(reset));
  or or_1 (or_1_out, m3_req_, m2_req_, m1_req_, m0_req_);

  // Notes on the sheet:
  //   BUS_OWNER_MASTER_0
  //   BUS_OWNER_MASTER_1
  //   BUS_OWNER_MASTER_2
  //   BUS_OWNER_MASTER_3
endmodule

module rom (
  input  reset,
  input  cs_,
  input  as_,
  input  [10:0] addr,
  output rdy_,
  output [31:0] rd_data
);

  wire and_1_out, clk_out;

  Clock clk (.out(clk_out));
  and and_1 (and_1_out, cs_, as_);
  Register #(.width(1)) register_1 (.D(and_1_out), .Q(rdy_), .clk(clk_out), .clr(reset));  // open: en
  ROM #(.addrWidth(11), .dataWidth(32)) rom_1 (.addr(addr), .data(rd_data), .sel(rdy_));

  // Notes on the sheet:
  //   contents of rom_1 (hex, n*v repeats v):
  //   0 11
endmodule

module spm (
  input  if_spm_as_,
  input  if_spm_rw,
  input  [10:0] if_spm_addr,
  input  [31:0] if_spm_wr_data,
  output [31:0] if_spm_rd_data
);

  wire and_1_out, clk_out, multiplexer_1_out, not_1_out, not_2_out, undriven, wea_q;
  wire [31:0] controlled_buffer_1_out;

  Clock clk (.out(clk_out));
  and and_1 (and_1_out, if_spm_as_, if_spm_rw);
  Multiplexer multiplexer_1 (.in0(1'b0), .in1(1'b1), .out(multiplexer_1_out), .sel(and_1_out));  // open: en
  Register #(.width(1)) wea (.D(multiplexer_1_out), .Q(wea_q), .clk(clk_out), .clr(undriven));  // open: en
  assign controlled_buffer_1_out = wea_q ? if_spm_wr_data : 32'bz;  // Controlled_Buffer controlled_buffer_1
  not not_1 (not_1_out, wea_q);
  not not_2 (not_2_out, wea_q);
  assign if_spm_rd_data = not_2_out ? controlled_buffer_1_out : 32'bz;  // Controlled_Buffer controlled_buffer_2
  RAM #(.addrWidth(11), .dataWidth(32)) ram_1 (
    .addr(if_spm_addr), .data(controlled_buffer_1_out), .sel(1'b1), .clk(clk_out), .ld(not_1_out));  // open: clr
endmodule

module if_reg (
  input  br_taken,
  input  flush,
  input  stall,
  input  [7:0] br_addr,
  input  [7:0] new_pc,
  input  [7:0] insn,
  input  reset,
  output [7:0] if_pc,
  output [7:0] if_insn,
  output if_en
);

  wire clk_out, multiplexer_3_out, multiplexer_6_out, nor_1_out, or_1_out, priority_encoder_1_out,
       xnor_1_out, xnor_2_out, xnor_3_out;
  wire [7:0] adder_1_out, multiplexer_1_out, multiplexer_2_out, multiplexer_4_out, multiplexer_5_out;

  Clock clk (.out(clk_out));
  xnor xnor_1 (xnor_1_out, 1'b0, stall);
  Adder adder_1 (.a(8'h1), .b(if_pc), .out(adder_1_out));  // open: cin, cout
  xnor xnor_2 (xnor_2_out, br_taken, 1'b1);
  xnor xnor_3 (xnor_3_out, flush, 1'b1);
  Priority_Encoder #(.select(1)) priority_encoder_1 (
    .in0(xnor_2_out), .in1(xnor_3_out), .out(priority_encoder_1_out), .en_in(xnor_1_out));  // open: gs, en_out
  Multiplexer #(.width(8)) multiplexer_1 (
    .in0(br_addr), .in1(new_pc), .out(multiplexer_1_out), .sel(priority_encoder_1_out), .en(or_1_out));
  Multiplexer #(.width(8)) multiplexer_2 (
    .in0(insn), .in1({8{1'b0}}), .out(multiplexer_2_out), .sel(priority_encoder_1_out), .en(or_1_out));
  Multiplexer multiplexer_3 (
    .in0(1'b1), .in1(1'b0), .out(multiplexer_3_out), .sel(priority_encoder_1_out), .en(or_1_out));
  nor nor_1 (nor_1_out, xnor_2_out, xnor_3_out);
  or or_1 (or_1_out, xnor_3_out, xnor_2_out);
  Multiplexer #(.width(8)) multiplexer_4 (
    .in0(multiplexer_1_out), .in1(adder_1_out), .out(multiplexer_4_out), .sel(nor_1_out), .en(xnor_1_out));
  Multiplexer #(.width(8)) multiplexer_5 (
    .in0(multiplexer_2_out), .in1(insn), .out(multiplexer_5_out), .sel(nor_1_out), .en(xnor_1_out));
  Multiplexer multiplexer_6 (
    .in0(multiplexer_3_out), .in1(1'b1), .out(multiplexer_6_out), .sel(nor_1_out), .en(xnor_1_out));
  Register u_if_pc (.D(multiplexer_4_out), .Q(if_pc), .clk(clk_out), .clr(reset));  // open: en
  Register u_if_insn (.D(multiplexer_5_out), .Q(if_insn), .clk(clk_out), .clr(reset));  // open: en
  Register #(.width(1)) u_if_en (.D(multiplexer_6_out), .Q(if_en), .clk(clk_out), .clr(reset));  // open: en

  // Notes on the sheet:
  //   ENABLE
  //   DISABLE
  //   ISA_NOP
endmodule

module buf_if (
  input  rw,
  input  as_,
  input  flush,
  input  stall,
  input  [2:0] s_index,
  input  spm_rd_data,
  input  bus_rdy_,
  input  bus_rd_data,
  input  rd_buf,
  input  [1:0] in_10,
  output spm_as_,
  output busy,
  output rd_data,
  output [1:0] out_14,
  output [1:0] out_15
);

  wire and_1_out, and_2_out, and_3_out, and_4_out, and_5_out, and_6_out, and_7_out, decoder_1_out0,
       decoder_1_out1, decoder_1_out2, decoder_1_out3, decoder_2_out0, decoder_2_out1, decoder_2_out2,
       decoder_2_out3, decoder_2_out4, decoder_2_out5, decoder_2_out6, decoder_2_out7, not_1_out, or_1_out,
       or_2_out, READ_ENABLE, STALL_DISABLE, STALL_ENABLE, undriven, xnor_2_out, xnor_4_out, xnor_5_out;
  wire [1:0] multiplexer_2_out, multiplexer_4_out, READ_ADDR;

  xnor xnor_1 (STALL_ENABLE, undriven, 1'b1);
  Multiplexer #(.select(2), .width(2)) multiplexer_1 (
    .in0(2'b00), .in1(2'b01), .in2(2'b10), .in3(2'b11), .out(out_14), .sel(out_15));  // open: en
  Decoder #(.select(2)) decoder_1 (
    .out0(decoder_1_out0), .out1(decoder_1_out1), .out2(decoder_1_out2), .out3(decoder_1_out3), .sel(in_10));  // open: en
  xnor xnor_2 (xnor_2_out, 1'b0, bus_rdy_);
  Register #(.width(2)) state (.D(out_14));  // open: en, Q, clk, clr
  xnor xnor_3 (READ_ENABLE, 1'b1, rw);
  xnor xnor_4 (xnor_4_out, as_, 1'b0);
  xnor xnor_5 (xnor_5_out, 1'b0, flush);
  xnor xnor_6 (STALL_DISABLE, stall, 1'b0);
  Decoder #(.select(3)) decoder_2 (
    .out0(decoder_2_out0), .out1(decoder_2_out1), .out2(decoder_2_out2), .out3(decoder_2_out3),
    .out4(decoder_2_out4), .out5(decoder_2_out5), .out6(decoder_2_out6), .out7(decoder_2_out7), .sel(s_index));  // open: en
  and and_1 (and_1_out, xnor_4_out, xnor_5_out, decoder_1_out0, STALL_DISABLE, decoder_2_out1);
  or or_1 (or_1_out, decoder_2_out0, decoder_2_out2, decoder_2_out3, decoder_2_out4, decoder_2_out5, decoder_2_out6, decoder_2_out7);
  and and_2 (and_2_out, decoder_1_out2, READ_ENABLE, xnor_2_out);
  Multiplexer #(.width(2)) multiplexer_2 (
    .in0(READ_ADDR), .in1(2'b10), .out(multiplexer_2_out), .sel(and_2_out));  // open: en
  Multiplexer multiplexer_3 (.in0(1'b1), .in1(1'b0), .out(spm_as_), .sel(and_1_out));  // open: en
  and and_3 (and_3_out, xnor_4_out, xnor_5_out, decoder_1_out1, or_1_out);
  not not_1 (not_1_out, xnor_2_out);
  and and_4 (and_4_out, decoder_1_out3, READ_ENABLE);
  and and_5 (and_5_out, READ_ENABLE, and_1_out);
  or or_2 (or_2_out, or_1_out, decoder_1_out1, and_6_out);
  and and_6 (and_6_out, decoder_1_out2, not_1_out);
  Multiplexer #(.width(2)) multiplexer_4 (
    .in0(multiplexer_2_out), .in1(2'b11), .out(multiplexer_4_out), .sel(and_4_out));  // open: en
  and and_7 (and_7_out, decoder_1_out3, STALL_DISABLE);
  Multiplexer #(.width(2)) multiplexer_5 (.in1(2'b01), .out(out_15), .sel(and_3_out));  // open: in0, en
  Multiplexer multiplexer_6 (.in0(1'b0), .in1(1'b1), .out(busy), .sel(or_2_out));  // open: en
  Multiplexer #(.width(2)) multiplexer_7 (.in1(2'b00), .out(out_15), .sel(and_7_out));  // open: in0, en
  Multiplexer #(.width(2)) multiplexer_8 (.in0(2'b00), .in1(2'b01), .out(READ_ADDR), .sel(and_5_out));  // open: en
  Multiplexer #(.select(2)) multiplexer_9 (
    .in0(1'b0), .in1(spm_rd_data), .in2(bus_rd_data), .in3(rd_buf), .out(rd_data), .sel(multiplexer_4_out));  // open: en

  // Other names for the same wires on the sheet: STATE[1:0] = in_10; STATE_FLAG[1:0] = out_15

  // Notes on the sheet:
  //   BUF_IF_STATE_IDLE
  //   BUF_IF_STATE_REQ
  //   BUF_IF_STATE_ACCESS
  //   BUF_IF_STATE_STALL
  //   READ
  //   HELLO
  //   ENABLE_
  //   DISABLE_
  //   ENABLE
endmodule

module bus_if_1 (
  input  stall,
  input  flush,
  input  [29:0] addr,
  input  as_,
  input  rw,
  input  [31:0] wr_data,
  input  [31:0] spm_rd_data,
  input  [31:0] bus_rd_data,
  input  bus_rdy_,
  input  bus_grnt_,
  input  [3:0] in_11,
  output busy,
  output [31:0] rd_data,
  output [29:0] spm_addr,
  output spm_as_,
  output spm_rw,
  output [31:0] spm_wr_data,
  output bus_req_,
  output [29:0] bus_addr,
  output bus_as_,
  output bus_rw,
  output [31:0] bus_wr_data,
  output [2:0] s_index,
  output [1:0] out_24
);

  wire and_1_out, and_2_out, and_3_out, and_4_out, and_8_out, and_9_out, and_11_out, and_12_out, and_13_out,
       and_14_out, BUF_IF_STATE_ACCESS, BUF_IF_STATE_IDLE, BUF_IF_STATE_REQ, BUF_IF_STATE_STALL, BUS_AS__t,
       BUS_GRNT_ENABLE, BUS_RDY_DISABLE, BUS_RDY_ENABLE, BUS_RDY_ENABLE_FIXED, BUS_REQ__t, BUS_RW_,
       BUS_SLAVE_1, BUS_SLAVE_1_FIXED, BUSY_t, clk, decoder_1_out0, decoder_1_out2, decoder_1_out3,
       decoder_1_out4, decoder_1_out5, decoder_1_out6, decoder_1_out7, FLUSH_DISABLE_AS_ENABLE,
       multiplexer_2_out, multiplexer_4_out, multiplexer_14_out, NOT_BUS_SLAVE_1, NOT_BUS_SLAVE_1_FIXED,
       or_2_out, or_3_out, READ_ENABLE, SPM_AS__t, STALL_DISABLE, STALL_ENABLE, xnor_1_out, xnor_3_out,
       xnor_4_out;
  wire [1:0] multiplexer_1_out, multiplexer_10_out, multiplexer_11_out, multiplexer_12_out, STATE;
  wire [29:0] BUS_ADDR_t, multiplexer_3_out;
  wire [31:0] BUS_WR_DATA_t, multiplexer_5_out, multiplexer_16_out, multiplexer_18_out, multiplexer_19_out,
       RD_BUF, RD_DATA_t;

  Clock clock_1 (.out(clk));
  BitSelector #(.width(30), .group(3)) bitselector_1 (.in(addr), .out(s_index), .sel(4'b1001));
  Decoder #(.select(3)) decoder_1 (
    .out0(decoder_1_out0), .out1(BUS_SLAVE_1), .out2(decoder_1_out2), .out3(decoder_1_out3),
    .out4(decoder_1_out4), .out5(decoder_1_out5), .out6(decoder_1_out6), .out7(decoder_1_out7), .sel(s_index));  // open: en
  Decoder #(.select(2)) decoder_2 (
    .out0(BUF_IF_STATE_IDLE), .out1(BUF_IF_STATE_REQ), .out2(BUF_IF_STATE_ACCESS), .out3(BUF_IF_STATE_STALL),
    .sel(STATE));  // open: en
  Multiplexer #(.select(2), .width(2)) multiplexer_1 (
    .in0(2'b00), .in1(2'b01), .in2(2'b10), .in3(2'b11), .out(multiplexer_1_out), .sel(out_24));  // open: en
  Multiplexer multiplexer_2 (.in0(1'b1), .in1(1'b0), .out(multiplexer_2_out), .sel(BUS_RDY_ENABLE_FIXED));  // open: en
  Multiplexer #(.width(30)) multiplexer_3 (
    .in0({30{1'b0}}), .in1({30{1'b0}}), .out(multiplexer_3_out), .sel(BUS_RDY_ENABLE_FIXED));  // open: en
  Multiplexer multiplexer_4 (.in0(1'b1), .in1(1'b1), .out(multiplexer_4_out), .sel(BUS_RDY_ENABLE_FIXED));  // open: en
  Multiplexer #(.width(32)) multiplexer_5 (
    .in0({32{1'b0}}), .in1({32{1'b0}}), .out(multiplexer_5_out), .sel(BUS_RDY_ENABLE_FIXED));  // open: en
  or or_1 (NOT_BUS_SLAVE_1, decoder_1_out0, decoder_1_out2, decoder_1_out3, decoder_1_out4, decoder_1_out5, decoder_1_out6, decoder_1_out7);
  Register #(.width(2)) status (.D(multiplexer_1_out), .en(1'b1), .Q(STATE), .clk(clk));  // open: clr
  Register #(.width(1)) register_1 (.D(BUSY_t), .Q(busy), .clk(clk));  // open: en, clr
  Register #(.width(32)) register_2 (.D(RD_DATA_t), .Q(rd_data), .clk(clk));  // open: en, clr
  Register #(.width(1)) register_3 (.D(SPM_AS__t), .Q(spm_as_), .clk(clk));  // open: en, clr
  Register #(.width(1)) register_4 (.D(BUS_REQ__t), .Q(bus_req_), .clk(clk));  // open: en, clr
  Register #(.width(30)) register_5 (.D(BUS_ADDR_t), .Q(bus_addr), .clk(clk));  // open: en, clr
  Register #(.width(1)) register_6 (.D(BUS_AS__t), .Q(bus_as_), .clk(clk));  // open: en, clr
  Register #(.width(1)) register_7 (.D(BUS_RW_), .Q(bus_rw), .clk(clk));  // open: en, clr
  Register #(.width(32)) register_8 (.D(BUS_WR_DATA_t), .Q(bus_wr_data), .clk(clk));  // open: en, clr
  and and_1 (and_1_out, BUF_IF_STATE_ACCESS, BUS_RDY_ENABLE, STALL_DISABLE);
  and and_2 (and_2_out, BUF_IF_STATE_STALL, STALL_DISABLE);
  Multiplexer multiplexer_6 (
    .in0(multiplexer_2_out), .in1(1'b1), .out(BUS_REQ__t), .sel(NOT_BUS_SLAVE_1_FIXED));  // open: en
  Multiplexer #(.width(30)) multiplexer_7 (
    .in0(multiplexer_3_out), .in1(addr), .out(BUS_ADDR_t), .sel(NOT_BUS_SLAVE_1_FIXED));  // open: en
  Multiplexer multiplexer_8 (
    .in0(multiplexer_4_out), .in1(rw), .out(BUS_RW_), .sel(NOT_BUS_SLAVE_1_FIXED));  // open: en
  Multiplexer #(.width(32)) multiplexer_9 (
    .in0(multiplexer_5_out), .in1(wr_data), .out(BUS_WR_DATA_t), .sel(NOT_BUS_SLAVE_1_FIXED));  // open: en
  Multiplexer #(.width(2)) multiplexer_10 (
    .in0(2'b00), .in1(2'b00), .out(multiplexer_10_out), .sel(or_2_out));  // open: en
  or or_2 (or_2_out, and_1_out, and_2_out);
  Multiplexer #(.width(2)) multiplexer_11 (
    .in0(multiplexer_10_out), .in1(2'b11), .out(multiplexer_11_out), .sel(and_3_out));  // open: en
  and and_3 (and_3_out, BUF_IF_STATE_ACCESS, BUS_RDY_ENABLE, STALL_ENABLE);
  Multiplexer #(.width(2)) multiplexer_12 (
    .in0(multiplexer_11_out), .in1(2'b10), .out(multiplexer_12_out), .sel(and_4_out));  // open: en
  and and_4 (and_4_out, BUF_IF_STATE_REQ, BUS_GRNT_ENABLE);
  Multiplexer #(.width(2)) multiplexer_13 (
    .in0(multiplexer_12_out), .in1(2'b01), .out(out_24), .sel(NOT_BUS_SLAVE_1_FIXED));  // open: en
  xnor xnor_1 (xnor_1_out, 1'b1, BUS_RW_);
  and and_5 (NOT_BUS_SLAVE_1_FIXED, BUF_IF_STATE_IDLE, FLUSH_DISABLE_AS_ENABLE, NOT_BUS_SLAVE_1);
  and and_6 (BUS_SLAVE_1_FIXED, BUF_IF_STATE_IDLE, FLUSH_DISABLE_AS_ENABLE, BUS_SLAVE_1);
  and and_7 (BUS_RDY_ENABLE_FIXED, BUF_IF_STATE_ACCESS, BUS_RDY_ENABLE);
  xnor xnor_2 (STALL_DISABLE, stall, 1'b0);
  xnor xnor_3 (xnor_3_out, as_, 1'b0);
  xnor xnor_4 (xnor_4_out, flush, 1'b0);
  xnor xnor_5 (BUS_GRNT_ENABLE, bus_grnt_, 1'b0);
  xnor xnor_6 (BUS_RDY_ENABLE, bus_rdy_, 1'b0);
  Multiplexer multiplexer_14 (.in0(1'b1), .in1(1'b1), .out(multiplexer_14_out), .sel(BUF_IF_STATE_ACCESS));  // open: en
  and and_8 (and_8_out, BUS_RDY_DISABLE, BUF_IF_STATE_ACCESS);
  xnor xnor_7 (READ_ENABLE, rw, 1'b1);
  and and_9 (and_9_out, BUS_SLAVE_1_FIXED, STALL_DISABLE);
  not not_1 (STALL_ENABLE, STALL_DISABLE);
  and and_10 (FLUSH_DISABLE_AS_ENABLE, xnor_3_out, xnor_4_out);
  not not_2 (BUS_RDY_DISABLE, BUS_RDY_ENABLE);
  Multiplexer multiplexer_15 (
    .in0(multiplexer_14_out), .in1(1'b0), .out(BUS_AS__t), .sel(BUS_GRNT_ENABLE));  // open: en
  and and_11 (and_11_out, xnor_1_out, BUS_RDY_ENABLE_FIXED);
  Multiplexer #(.width(32)) multiplexer_16 (
    .in0({32{1'b0}}), .in1(RD_BUF), .out(multiplexer_16_out), .sel(and_12_out));  // open: en
  and and_12 (and_12_out, BUF_IF_STATE_STALL, READ_ENABLE);
  Multiplexer multiplexer_17 (.in0(1'b1), .in1(1'b0), .out(SPM_AS__t), .sel(and_9_out));  // open: en
  or or_3 (or_3_out, NOT_BUS_SLAVE_1_FIXED, BUF_IF_STATE_REQ, and_8_out);
  Multiplexer #(.width(32)) multiplexer_18 (
    .in0({32{1'b0}}), .in1(bus_rd_data), .out(multiplexer_18_out), .sel(and_11_out));  // open: en
  and and_13 (and_13_out, BUS_RDY_ENABLE_FIXED, READ_ENABLE);
  Register #(.width(32)) u_rd_buf (.D(multiplexer_18_out), .Q(RD_BUF), .clk(clk));  // open: en, clr
  Multiplexer #(.width(32)) multiplexer_19 (
    .in0(multiplexer_16_out), .in1(bus_rd_data), .out(multiplexer_19_out), .sel(and_13_out));  // open: en
  and and_14 (and_14_out, and_9_out, READ_ENABLE);
  Multiplexer #(.width(32)) multiplexer_20 (
    .in0(multiplexer_19_out), .in1(spm_rd_data), .out(RD_DATA_t), .sel(and_14_out));  // open: en
  Multiplexer multiplexer_21 (.in0(1'b0), .in1(1'b1), .out(BUSY_t), .sel(or_3_out));  // open: en

  assign spm_addr = addr;
  assign spm_rw = rw;
  assign spm_wr_data = wr_data;

  // Other names for the same wires on the sheet: BUS_RDY = bus_rdy_; SPM_RW_ = rw; STATE_FLAG[1:0] = out_24

  // Notes on the sheet:
  //   ENABLE_
  //   DISABLE_
  //   ENABLE
  //   DISABLE
  //   BUF_IF_STATE_ACCESS
  //   READ
  //   BUF_IF_STATE_IDLE
  //   BUF_IF_STATE_REQ
  //   BUF_IF_STATE_STALL
  //   READ
  //   READ
endmodule

module bus_if_0 (
  input  stall,
  input  flush,
  input  [3:0] addr,
  input  as_,
  input  rw,
  input  [7:0] wr_data,
  input  [7:0] spm_rd_data,
  input  [7:0] bus_rd_data,
  input  bus_rdy_,
  input  bus_grnt_,
  output [1:0] out_11,
  output [1:0] out_12,
  output busy,
  output [7:0] rd_data,
  output [3:0] spm_addr,
  output spm_as_,
  output spm_rw,
  output [7:0] spm_wr_data,
  output bus_req_,
  output [3:0] bus_addr,
  output bus_as_,
  output bus_rw,
  output [7:0] bus_wr_data,
  output [1:0] out_24,
  output [1:0] out_25,
  output [2:0] out_26
);

  wire and_5_out, and_6_out, and_7_out, and_8_out, and_9_out, and_11_out, and_12_out, and_13_out, and_14_out,
       and_15_out, and_16_out, and_17_out, BUF_IF_STATE_ACCESS, BUF_IF_STATE_ACCESS_BUS_RDY_ENABLE,
       BUF_IF_STATE_ACCESS_READ_DISABLE, BUF_IF_STATE_IDLE, BUF_IF_STATE_IDLE_FIXED,
       BUF_IF_STATE_IDLE_NOT_BUS_SLAVE_1, BUF_IF_STATE_REQ, BUF_IF_STATE_STALL, BUS_AS__t, BUS_GRNT_ENABLE,
       BUS_RDY_DISABLE, BUS_RDY_ENABLE, BUS_REQ__t, BUS_RW_IN, BUS_SLAVE_1, BUSY_t, clk, decoder_2_out0,
       decoder_2_out2, decoder_2_out3, decoder_2_out4, decoder_2_out5, decoder_2_out6, decoder_2_out7,
       FLUSH_DISABLE_AS_ENABLE, multiplexer_2_out, multiplexer_7_out, multiplexer_9_out, NOT_BUS_SLAVE_1,
       or_2_out, or_3_out, READ_DISABLE, READ_ENABLE, SPM_AS__t, STALL_DISABLE, STALL_ENABLE, xnor_4_out,
       xnor_5_out, xnor_7_out;
  wire [1:0] multiplexer_3_out, multiplexer_10_out, multiplexer_14_out;
  wire [3:0] BUS_ADDR_t, multiplexer_8_out;
  wire [7:0] BUS_WR_DATA_t, multiplexer_6_out, RD_BUF_IN, RD_BUF_OUT, RD_DATA_FOR_BUS_RD_DATA,
       RD_DATA_FOR_RD_BUF, RD_DATA_t;

  Clock clock_1 (.out(clk));
  Register rd_buf (.D(RD_BUF_IN), .Q(RD_BUF_OUT), .clk(clk));  // open: en, clr
  Decoder #(.select(2)) decoder_1 (
    .out0(BUF_IF_STATE_IDLE), .out1(BUF_IF_STATE_REQ), .out2(BUF_IF_STATE_ACCESS), .out3(BUF_IF_STATE_STALL),
    .sel(out_12));  // open: en
  BitSelector #(.width(4), .group(3)) bitselector_1 (.in(addr), .out(out_26), .sel(1'b1));
  xnor xnor_1 (BUS_RDY_ENABLE, bus_rdy_, 1'b0);
  xnor xnor_2 (READ_ENABLE, rw, 1'b1);
  xnor xnor_3 (STALL_DISABLE, stall, 1'b0);
  xnor xnor_4 (xnor_4_out, as_, 1'b0);
  xnor xnor_5 (xnor_5_out, flush, 1'b0);
  Multiplexer #(.select(2), .width(2)) multiplexer_1 (
    .in0(2'b00), .in1(2'b01), .in2(2'b10), .in3(2'b11));  // open: out, sel, en
  Decoder #(.select(3)) decoder_2 (
    .out0(decoder_2_out0), .out1(BUS_SLAVE_1), .out2(decoder_2_out2), .out3(decoder_2_out3),
    .out4(decoder_2_out4), .out5(decoder_2_out5), .out6(decoder_2_out6), .out7(decoder_2_out7), .sel(out_26));  // open: en
  not not_1 (BUS_RDY_DISABLE, BUS_RDY_ENABLE);
  not not_2 (READ_DISABLE, READ_ENABLE);
  and and_1 (FLUSH_DISABLE_AS_ENABLE, xnor_4_out, xnor_5_out);
  and and_2 (BUF_IF_STATE_IDLE_FIXED, BUF_IF_STATE_IDLE, FLUSH_DISABLE_AS_ENABLE, BUS_SLAVE_1);
  and and_3 (BUF_IF_STATE_IDLE_NOT_BUS_SLAVE_1, BUF_IF_STATE_IDLE, FLUSH_DISABLE_AS_ENABLE, NOT_BUS_SLAVE_1);
  and and_4 (BUF_IF_STATE_ACCESS_BUS_RDY_ENABLE, BUF_IF_STATE_ACCESS, BUS_RDY_ENABLE);
  xnor xnor_6 (BUS_GRNT_ENABLE, bus_grnt_, 1'b0);
  Register #(.width(1)) register_1 (.D(SPM_AS__t), .Q(spm_as_), .clk(clk));  // open: en, clr
  not not_3 (STALL_ENABLE, STALL_DISABLE);
  Register #(.width(2)) status (.D(out_11), .en(1'b1), .Q(out_12), .clk(clk));  // open: clr
  or or_1 (NOT_BUS_SLAVE_1, decoder_2_out0, decoder_2_out2, decoder_2_out3, decoder_2_out4, decoder_2_out5, decoder_2_out6, decoder_2_out7);
  Register #(.width(1)) register_2 (.D(BUSY_t), .Q(busy), .clk(clk));  // open: en, clr
  Register register_3 (.D(RD_DATA_t), .Q(rd_data), .clk(clk));  // open: en, clr
  Register #(.width(1)) register_4 (.D(BUS_REQ__t), .Q(bus_req_), .clk(clk));  // open: en, clr
  Register #(.width(4)) register_5 (.D(BUS_ADDR_t), .Q(bus_addr), .clk(clk));  // open: en, clr
  Register #(.width(1)) register_6 (.D(BUS_AS__t), .Q(bus_as_), .clk(clk));  // open: en, clr
  Register #(.width(1)) register_7 (.D(BUS_RW_IN), .Q(bus_rw), .clk(clk));  // open: en, clr
  Register register_8 (.D(BUS_WR_DATA_t), .Q(bus_wr_data), .clk(clk));  // open: en, clr
  and and_5 (and_5_out, BUF_IF_STATE_STALL, STALL_DISABLE);
  and and_6 (and_6_out, BUF_IF_STATE_ACCESS, BUS_RDY_ENABLE);
  and and_7 (and_7_out, BUF_IF_STATE_ACCESS, BUS_RDY_ENABLE);
  and and_8 (and_8_out, STALL_DISABLE, and_6_out);
  Multiplexer multiplexer_2 (.in0(1'b1), .in1(1'b1), .out(multiplexer_2_out), .sel(BUF_IF_STATE_ACCESS));  // open: en
  and and_9 (and_9_out, BUF_IF_STATE_IDLE_FIXED, STALL_DISABLE);
  and and_10 (BUF_IF_STATE_ACCESS_READ_DISABLE, BUF_IF_STATE_ACCESS, BUS_RDY_DISABLE);
  and and_11 (and_11_out, BUF_IF_STATE_STALL, READ_ENABLE);
  Multiplexer #(.width(2)) multiplexer_3 (
    .in0(out_12), .in1(2'b00), .out(multiplexer_3_out), .sel(or_2_out));  // open: en
  or or_2 (or_2_out, and_5_out, and_8_out);
  and and_12 (and_12_out, and_6_out, STALL_ENABLE);
  xnor xnor_7 (xnor_7_out, bus_rw, 1'b1);
  Multiplexer multiplexer_4 (.in0(1'b1), .in1(1'b0), .out(SPM_AS__t), .sel(and_9_out));  // open: en
  or or_3 (or_3_out, BUF_IF_STATE_IDLE_FIXED, BUF_IF_STATE_REQ, BUF_IF_STATE_ACCESS_READ_DISABLE);
  Multiplexer #(.width(8)) multiplexer_5 (
    .in0({8{1'b0}}), .in1(RD_BUF_OUT), .out(RD_DATA_FOR_RD_BUF), .sel(and_11_out));  // open: en
  Multiplexer #(.width(8)) multiplexer_6 (
    .in0({8{1'b0}}), .in1({8{1'b0}}), .out(multiplexer_6_out), .sel(BUF_IF_STATE_ACCESS_BUS_RDY_ENABLE));  // open: en
  Multiplexer multiplexer_7 (
    .in0(1'b1), .in1(1'b1), .out(multiplexer_7_out), .sel(BUF_IF_STATE_ACCESS_BUS_RDY_ENABLE));  // open: en
  Multiplexer #(.width(4)) multiplexer_8 (
    .in0(4'b0000), .in1(4'b0000), .out(multiplexer_8_out), .sel(BUF_IF_STATE_ACCESS_BUS_RDY_ENABLE));  // open: en
  Multiplexer multiplexer_9 (
    .in0(1'b1), .in1(1'b1), .out(multiplexer_9_out), .sel(BUF_IF_STATE_ACCESS_BUS_RDY_ENABLE));  // open: en
  Multiplexer #(.width(2)) multiplexer_10 (
    .in0(multiplexer_3_out), .in1(2'b11), .out(multiplexer_10_out), .sel(and_12_out));  // open: en
  and and_13 (and_13_out, BUF_IF_STATE_REQ, BUS_GRNT_ENABLE);
  and and_14 (and_14_out, BUF_IF_STATE_REQ, BUS_GRNT_ENABLE);
  Multiplexer #(.width(8)) multiplexer_11 (
    .in0(RD_DATA_FOR_BUS_RD_DATA), .in1(spm_rd_data), .out(RD_DATA_t), .sel(and_15_out));  // open: en
  and and_15 (and_15_out, READ_ENABLE, and_9_out);
  Multiplexer multiplexer_12 (.in0(1'b0), .in1(1'b1), .out(BUSY_t), .sel(or_3_out));  // open: en
  Multiplexer #(.width(8)) multiplexer_13 (
    .in0(RD_DATA_FOR_RD_BUF), .in1(bus_rd_data), .out(RD_DATA_FOR_BUS_RD_DATA), .sel(and_16_out));  // open: en
  and and_16 (and_16_out, and_7_out, READ_ENABLE);
  Multiplexer #(.width(2)) multiplexer_14 (
    .in0(multiplexer_10_out), .in1(2'b10), .out(multiplexer_14_out), .sel(and_13_out));  // open: en
  Multiplexer multiplexer_15 (.in0(multiplexer_2_out), .in1(1'b0), .out(BUS_AS__t), .sel(and_14_out));  // open: en
  Multiplexer #(.width(8)) multiplexer_16 (
    .in0({8{1'b0}}), .in1(bus_rd_data), .out(RD_BUF_IN), .sel(and_17_out));  // open: en
  and and_17 (and_17_out, BUF_IF_STATE_ACCESS, xnor_7_out);
  Multiplexer #(.width(8)) multiplexer_17 (
    .in0(multiplexer_6_out), .in1(wr_data), .out(BUS_WR_DATA_t), .sel(BUF_IF_STATE_IDLE_NOT_BUS_SLAVE_1));  // open: en
  Multiplexer multiplexer_18 (
    .in0(multiplexer_7_out), .in1(rw), .out(BUS_RW_IN), .sel(BUF_IF_STATE_IDLE_NOT_BUS_SLAVE_1));  // open: en
  Multiplexer #(.width(4)) multiplexer_19 (
    .in0(multiplexer_8_out), .in1(addr), .out(BUS_ADDR_t), .sel(BUF_IF_STATE_IDLE_NOT_BUS_SLAVE_1));  // open: en
  Multiplexer multiplexer_20 (
    .in0(multiplexer_9_out), .in1(1'b0), .out(BUS_REQ__t), .sel(BUF_IF_STATE_IDLE_NOT_BUS_SLAVE_1));  // open: en
  Multiplexer #(.width(2)) multiplexer_21 (
    .in0(multiplexer_14_out), .in1(2'b01), .out(out_11), .sel(BUF_IF_STATE_IDLE_NOT_BUS_SLAVE_1));  // open: en

  assign out_24 = out_11;
  assign out_25 = out_11;
  assign spm_addr = addr;
  assign spm_rw = rw;
  assign spm_wr_data = wr_data;

  // Other names for the same wires on the sheet: BUS_RDY = bus_rdy_; BUS_RW_OUT = bus_rw; SPM_RW_ = rw;
  //   STATE_IN[1:0] = out_11; STATE_OUT[1:0] = out_12

  // Notes on the sheet:
  //   READ
  //   BUF_IF_STATE_IDLE
  //   BUF_IF_STATE_REQ
  //   BUF_IF_STATE_ACCESS
  //   BUF_IF_STATE_STALL
  //   ENABLE_
  //   DISABLE_
  //   ENABLE
  //   DISABLE
  //   BUF_IF_STATE_ACCESS
  //   BUF_IF_STATE_IDLE
  //   BUF_IF_STATE_STALL
  //   BUF_IF_STATE_REQ
endmodule

module arbiter_1 (
  input  m0_grnt_,
  input  m1_grnt_,
  input  m2_grnt_,
  input  m3_grnt_,
  input  [1:0] owner
);

  Demultiplexer #(.select(2)) demultiplexer_1 (
    .out0(m0_grnt_), .out1(m1_grnt_), .out2(m2_grnt_), .out3(m3_grnt_), .in(1'b1), .sel(owner), .en(1'b1));

  // Notes on the sheet:
  //   ENABLE_
endmodule

module arbiter_2 (
  input  m3_req_,
  input  m2_req_,
  input  m1_req_,
  input  m0_req_,
  input  reset,
  output [1:0] out_6,
  output [1:0] out_7,
  output [1:0] out_8,
  output [1:0] out_9,
  output [1:0] out_10,
  output m0_grnt_,
  output [1:0] out_12,
  output m1_grnt_,
  output [1:0] out_14,
  output m2_grnt_,
  output m3_grnt_
);

  wire clock_out, demultiplexer_1_out0, demultiplexer_1_out1, demultiplexer_1_out2, demultiplexer_1_out3, sel;
  wire [1:0] priority_encoder_1_out, priority_encoder_2_out, priority_encoder_3_out, priority_encoder_4_out;

  Clock clock (.out(clock_out));
  Demultiplexer #(.select(2)) demultiplexer_1 (
    .out0(demultiplexer_1_out0), .out1(demultiplexer_1_out1), .out2(demultiplexer_1_out2),
    .out3(demultiplexer_1_out3), .in(1'b1), .sel(out_14), .en(1'b1));
  Register #(.width(2)) register_1 (.D(out_6), .Q(out_14), .clk(clock_out), .clr(reset));  // open: en
  Priority_Encoder #(.select(2)) priority_encoder_1 (
    .in0(m3_req_), .in1(m2_req_), .in2(m1_req_), .in3(m0_req_), .out(priority_encoder_1_out),
    .en_in(demultiplexer_1_out0));  // open: gs, en_out
  Multiplexer #(.select(2), .width(2)) multiplexer_1 (
    .in0(2'b11), .in1(2'b10), .in2(2'b01), .in3(2'b00), .out(out_7), .sel(priority_encoder_1_out));  // open: en
  Multiplexer #(.select(2), .width(2)) multiplexer_2 (
    .in0(2'b00), .in1(2'b11), .in2(2'b10), .in3(2'b01), .out(out_7), .sel(priority_encoder_2_out));  // open: en
  Priority_Encoder #(.select(2)) priority_encoder_2 (
    .in0(m0_req_), .in1(m3_req_), .in2(m2_req_), .in3(m1_req_), .out(priority_encoder_2_out),
    .en_in(demultiplexer_1_out1));  // open: gs, en_out
  Multiplexer #(.select(2), .width(2)) multiplexer_3 (
    .in0(2'b01), .in1(2'b00), .in2(2'b11), .in3(2'b10), .out(out_7), .sel(priority_encoder_3_out));  // open: en
  Priority_Encoder #(.select(2)) priority_encoder_3 (
    .in0(m1_req_), .in1(m0_req_), .in2(m3_req_), .in3(m2_req_), .out(priority_encoder_3_out),
    .en_in(demultiplexer_1_out2));  // open: gs, en_out
  Multiplexer #(.select(2), .width(2)) multiplexer_4 (
    .in0(2'b10), .in1(2'b01), .in2(2'b00), .in3(2'b11), .out(out_7), .sel(priority_encoder_4_out));  // open: en
  Priority_Encoder #(.select(2)) priority_encoder_4 (
    .in0(m2_req_), .in1(m1_req_), .in2(m0_req_), .in3(m3_req_), .out(priority_encoder_4_out),
    .en_in(demultiplexer_1_out3));  // open: gs, en_out
  or or_1 (sel, m3_req_, m2_req_, m1_req_, m0_req_);
  and and_1 (m0_grnt_, demultiplexer_1_out0, sel);
  and and_2 (m1_grnt_, demultiplexer_1_out1, sel);
  and and_3 (m2_grnt_, demultiplexer_1_out2, sel);
  and and_4 (m3_grnt_, demultiplexer_1_out3, sel);
  Multiplexer #(.width(2)) multiplexer_5 (.in0(2'b00), .in1(out_7), .out(out_6), .sel(sel));  // open: en

  assign out_8 = out_7;
  assign out_9 = out_7;
  assign out_10 = out_7;
  assign out_12 = out_6;

  // Other names for the same wires on the sheet: owner[1:0] = out_6

  // Notes on the sheet:
  //   BUS_OWNER_MASTER_0
  //   BUS_OWNER_MASTER_1
  //   BUS_OWNER_MASTER_2
  //   BUS_OWNER_MASTER_3
  //   ENABLE_
endmodule
